// Digital circuit intcode.dig as structural Verilog
module intcode (
  input  clock
);

  wire and_1_out, and_2_out, and_3_out, and_4_out, and_5_out, comparator_1_eq, comparator_2_eq,
       comparator_3_eq, decoder_1_out_0, decoder_1_out_1, decoder_1_out_2, decoder_1_out_3, nor_1_out,
       nor_2_out, run_q, sub_1_c_o, sub_2_c_o;
  wire [1:0] phase_out;
  wire [15:0] add_1_s, add_2_s, pc_q, ram_d2;
  wire [31:0] cycles_out, icount_out, Y_q;
  wire [63:0] at_0_q, instr_q, mul_mul, multiplexer_1_out, multiplexer_2_out, multiplexer_3_out,
       multiplexer_4_out, plus_s, ram_d1, sub_1_s, sub_2_s, X_q;
  wire [63:16] ram_d2_2;
  wire [63:32] Y_q_2;

  // Probe on at_0_q
  LED running (.in(run_q));
  and and_1 (and_1_out, run_q, clock);
  Register #(.Bits(64)) at_0 (.D(multiplexer_4_out), .C(and_1_out), .en(and_2_out), .Q(at_0_q));
  Counter #(.Bits(32)) cycles (.en(run_q), .C(and_1_out), .clr(1'b0), .out(cycles_out));  // open: ovf
  and and_2 (and_2_out, comparator_1_eq, decoder_1_out_3);
  T_FF #(.Default(1)) run (.T(and_5_out), .C(and_1_out), .Q(run_q));  // open: nQ
  // Probe on cycles_out
  Comparator #(.Bits(16)) comparator_1 (.a({16{1'b0}}), .b(ram_d2), .eq(comparator_1_eq));  // open: gt, lt
  Add #(.Bits(16)) add_1 (.a({{14{1'b0}}, phase_out}), .b(pc_q), .c_i(1'b0), .s(add_1_s));  // open: c_o
  RAMDualAccess #(.AddrBits(16), .Bits(64), .isProgramMemory("true")) ram (
    .str(decoder_1_out_3), .C(and_1_out), .ld(1'b1), .A1(ram_d2), .Din1(multiplexer_4_out), .A2(add_1_s),
    .D1(ram_d1), .D2({ram_d2_2, ram_d2}));
  Add #(.Bits(16)) add_2 (.a(pc_q), .b({{14{1'b0}}, phase_out}), .c_i(1'b1), .s(add_2_s));  // open: c_o
  Register #(.Bits(16), .isProgramCounter("true")) pc (.D(add_2_s), .C(and_1_out), .en(decoder_1_out_3), .Q(pc_q));
  // Probe on pc_q
  Counter #(.Bits(32)) icount (.en(decoder_1_out_0), .C(and_1_out), .clr(1'b0), .out(icount_out));  // open: ovf
  Counter #(.Bits(2)) phase (.en(1'b1), .C(and_1_out), .clr(decoder_1_out_3), .out(phase_out));  // open: ovf
  // Probe on icount_out
  Register #(.Bits(64)) instr (.D({ram_d2_2, ram_d2}), .C(and_1_out), .en(decoder_1_out_0), .Q(instr_q));
  // Probe on phase_out
  // Probe on instr_q
  Decoder #(.Selector_Bits(2)) decoder_1 (
    .sel(phase_out), .out_0(decoder_1_out_0), .out_1(decoder_1_out_1), .out_2(decoder_1_out_2),
    .out_3(decoder_1_out_3));
  Sub #(.Bits(64)) sub_1 (.a(instr_q), .b(64'h3e8), .c_i(1'b0), .s(sub_1_s), .c_o(sub_1_c_o));
  and and_3 (and_3_out, ~sub_1_c_o, decoder_1_out_2);  // And
  Multiplexer #(.Bits(64)) multiplexer_1 (.sel(sub_1_c_o), .in_0(sub_1_s), .in_1(instr_q), .out(multiplexer_1_out));
  Sub #(.Bits(64)) sub_2 (.a(multiplexer_1_out), .b(64'h64), .c_i(1'b0), .s(sub_2_s), .c_o(sub_2_c_o));
  and and_4 (and_4_out, ~sub_2_c_o, decoder_1_out_1);  // And
  Multiplexer #(.Bits(64)) multiplexer_2 (
    .sel(sub_2_c_o), .in_0(sub_2_s), .in_1(multiplexer_1_out), .out(multiplexer_2_out));
  nor nor_1 (nor_1_out, and_3_out, and_4_out);
  Multiplexer #(.Bits(64)) multiplexer_3 (
    .sel(nor_1_out), .in_0({ram_d2_2, ram_d2}), .in_1(ram_d1), .out(multiplexer_3_out));
  and and_5 (and_5_out, decoder_1_out_1, nor_2_out);
  Comparator #(.Signed("true"), .Bits(64)) comparator_2 (
    .a(multiplexer_2_out), .b(64'h1), .eq(comparator_2_eq));  // open: gt, lt
  Register #(.Bits(64)) X (.D(multiplexer_3_out), .C(and_1_out), .en(decoder_1_out_1), .Q(X_q));
  Add #(.Bits(64)) plus (.a(X_q), .b({Y_q_2, Y_q}), .c_i(1'b0), .s(plus_s));  // open: c_o
  nor nor_2 (nor_2_out, comparator_2_eq, comparator_3_eq);
  Comparator #(.Signed("true"), .Bits(64)) comparator_3 (
    .a(multiplexer_2_out), .b(64'h2), .eq(comparator_3_eq));  // open: gt, lt
  // Probe on X_q
  Register #(.Bits(64)) Y (.D(multiplexer_3_out), .C(and_1_out), .en(decoder_1_out_2), .Q({Y_q_2, Y_q}));
  Mul #(.Bits(32), .Signed("true")) mul (.a(Y_q), .b(X_q[31:0]), .mul(mul_mul));
  // Probe on {Y_q_2, Y_q}
  Multiplexer #(.Bits(64)) multiplexer_4 (
    .sel(comparator_3_eq), .in_0(plus_s), .in_1(mul_mul), .out(multiplexer_4_out));
  // Probe r on multiplexer_4_out

  // Notes on the sheet:
  //   clock: Hz: 100
  //   Instruction decoding
  //   Internal registers
  //   ALU
endmodule
